// Logisim project mips.circ as structural Verilog: 6 circuits, main circuit main
module main (
);

  wire and_1_out, clk, uc_1_branch, uc_1_jump, uc_1_mem_to_reg, uc_1_mem_write, uc_1_reg_dest,
       uc_1_reg_write, uc_1_ula_src, ula_1_zero;
  wire [4:0] multiplexer_1_out;
  wire [5:0] ula_control_1_out_3;
  wire [6:0] uc_1_alu_op;
  wire [27:0] bit_extender_1_out, shifter_1_out;
  wire [31:0] adder_1_out, adder_2_out, bit_extender_2_out, br_1_br_rs, br_1_br_rs_2, multiplexer_2_out,
       multiplexer_3_out, multiplexer_4_out, multiplexer_5_out, ram_1_data, ram_2_data, register_1_q,
       shifter_2_out, ula_1_out_5;

  Register #(.width(32), .Select("low")) register_1 (
    .D(multiplexer_4_out), .Q(register_1_q), .clk(clk));  // open: en, clr
  Adder #(.width(32)) adder_1 (.a(register_1_q), .b(32'h4), .out(adder_1_out));  // open: cin, cout
  RAM #(.addrWidth(24), .dataWidth(32), .Select("low")) ram_1 (
    .addr(register_1_q[25:2]), .data(ram_1_data), .clk(clk));  // open: sel, ld, clr
  assign bit_extender_1_out = {{2{1'b0}}, ram_1_data[25:0]};  // Bit_Extender bit_extender_1
  Shifter #(.width(28)) shifter_1 (.in(bit_extender_1_out), .\dist (5'b00010), .out(shifter_1_out));
  Multiplexer #(.width(5), .enable("false")) multiplexer_1 (
    .in0(ram_1_data[20:16]), .in1(ram_1_data[15:11]), .out(multiplexer_1_out), .sel(uc_1_reg_dest));
  UC uc_1 (
    .in_1(ram_1_data[31:26]), .reg_write(uc_1_reg_write), .reg_dest(uc_1_reg_dest),
    .mem_to_reg(uc_1_mem_to_reg), .ula_src(uc_1_ula_src), .alu_op(uc_1_alu_op), .mem_write(uc_1_mem_write),
    .jump(uc_1_jump), .branch(uc_1_branch));
  BR br_1 (
    .rs(ram_1_data[25:21]), .rt(ram_1_data[20:16]), .rd(multiplexer_1_out), .BR_RS(br_1_br_rs),
    .BR_RS_2(br_1_br_rs_2), .reg_write(uc_1_reg_write), .clk(clk), .data(multiplexer_5_out));
  assign bit_extender_2_out = {{16{ram_1_data[15]}}, ram_1_data[15:0]};  // Bit_Extender bit_extender_2
  Shifter #(.width(32)) shifter_2 (.in(bit_extender_2_out), .\dist (5'b00010), .out(shifter_2_out));
  Multiplexer #(.width(32), .enable("false")) multiplexer_2 (
    .in0(br_1_br_rs_2), .in1(bit_extender_2_out), .out(multiplexer_2_out), .sel(uc_1_ula_src));
  ULA ula_1 (
    .in_1(br_1_br_rs), .in_2(multiplexer_2_out), .out_5(ula_1_out_5), .in_3(ula_control_1_out_3),
    .zero(ula_1_zero));
  ula_control ula_control_1 (.uc_op(uc_1_alu_op), .funct(ram_1_data[5:0]), .out_3(ula_control_1_out_3));
  Multiplexer #(.width(32), .enable("false")) multiplexer_3 (
    .in0(adder_1_out), .in1({adder_1_out[31:28], shifter_1_out}), .out(multiplexer_3_out), .sel(uc_1_jump));
  Adder #(.width(32)) adder_2 (.a(adder_1_out), .b(shifter_2_out), .out(adder_2_out));  // open: cin, cout
  Multiplexer #(.width(32), .enable("false")) multiplexer_4 (
    .in0(multiplexer_3_out), .in1(adder_2_out), .out(multiplexer_4_out), .sel(and_1_out));
  and and_1 (and_1_out, uc_1_branch, ula_1_zero);
  Clock clock_1 (.out(clk));
  RAM #(.addrWidth(24), .dataWidth(32), .bus("separate"), .simpleMode("false"), .Select("low")) ram_2 (
    .addr(ula_1_out_5[23:0]), .din(br_1_br_rs_2), .data(ram_2_data), .str(uc_1_mem_write), .clk(clk));  // open: sel, ld, clr
  Multiplexer #(.width(32), .enable("false")) multiplexer_5 (
    .in0(ula_1_out_5), .in1(ram_2_data), .out(multiplexer_5_out), .sel(uc_1_mem_to_reg));
endmodule

module BR (
  input  reg_write,
  input  [4:0] rs,
  input  [4:0] rt,
  input  [4:0] rd,
  input  [31:0] data,
  input  clk,
  output [31:0] BR_RS,
  output [31:0] BR_RS_2
);

  wire demultiplexer_1_out0, demultiplexer_1_out1, demultiplexer_1_out2, undriven;
  wire [31:0] register_1_q, register_2_q, register_4_q, register_5_q, register_10_q;

  Demultiplexer #(.select(2), .enable("false")) demultiplexer_1 (
    .out0(demultiplexer_1_out0), .out1(demultiplexer_1_out1), .out2(demultiplexer_1_out2), .in(reg_write),
    .sel(rd[1:0]));  // open: out3
  Register #(.width(32), .Select("low")) register_1 (.D(data), .Q(register_1_q), .clk(clk));  // open: en, clr
  Register #(.width(32), .Select("low")) register_2 (.D(data), .Q(register_2_q), .clk(clk));  // open: en, clr
  Register #(.width(32), .Select("low")) register_3 (.clk(undriven));  // open: D, en, Q, clr
  Register #(.width(32), .Select("low")) register_4 (
    .D(data), .en(demultiplexer_1_out1), .Q(register_4_q), .clk(clk));  // open: clr
  Register #(.width(32), .Select("low")) register_5 (
    .D(data), .en(demultiplexer_1_out2), .Q(register_5_q), .clk(clk));  // open: clr
  Register #(.width(32), .Select("low")) register_6 (.clk(clk));  // open: D, en, Q, clr
  Register #(.width(32), .Select("low")) register_7 (.clk(clk));  // open: D, en, Q, clr
  Register #(.width(32), .Select("low")) register_8 ();  // open: D, en, Q, clk, clr
  Register #(.width(32), .Select("low")) register_9 ();  // open: D, en, Q, clk, clr
  Register #(.width(32), .Select("low")) register_10 (.D(data), .Q(register_10_q), .clk(clk));  // open: en, clr
  Register #(.width(32), .Select("low")) register_11 (.clk(clk));  // open: D, en, Q, clr
  Register #(.width(32), .Select("low")) register_12 ();  // open: D, en, Q, clk, clr
  Multiplexer #(.select(3), .width(32), .enable("false")) multiplexer_1 (
    .in0(register_1_q), .in1(register_4_q), .in2(register_5_q), .in3(register_10_q), .in4(register_2_q),
    .out(BR_RS), .sel(rs[2:0]));  // open: in5, in6, in7
  Multiplexer #(.select(3), .width(32), .enable("false")) multiplexer_2 (
    .in0(register_1_q), .in1(register_4_q), .in2(register_5_q), .in3(register_10_q), .in4(register_2_q),
    .out(BR_RS_2), .sel(rt[2:0]));  // open: in5, in6, in7
endmodule

module ULA (
  input  [31:0] in_1,
  input  [31:0] in_2,
  input  [5:0] in_3,
  output zero,
  output [31:0] out_5
);

  wire adder_1_cout, subtractor_1_bout;
  wire [31:0] adder_1_out, divider_1_out, divider_1_rem, multiplier_1_cout, multiplier_1_out,
       subtractor_1_out;

  Comparator #(.width(32)) comparator_1 (.a(in_1), .b(in_2), .eq(zero));  // open: gt, lt
  Adder #(.width(32)) adder_1 (.a(in_1), .b(in_2), .out(adder_1_out), .cout(adder_1_cout));  // open: cin
  Subtractor #(.width(32)) subtractor_1 (
    .a(in_1), .b(in_2), .out(subtractor_1_out), .bout(subtractor_1_bout));  // open: bin
  Multiplier #(.width(32)) multiplier_1 (
    .a(in_1), .b(in_2), .out(multiplier_1_out), .cout(multiplier_1_cout));  // open: cin
  Divider #(.width(32)) divider_1 (.a(in_1), .b(in_2), .out(divider_1_out), .rem(divider_1_rem));  // open: upper
  Multiplexer #(.select(2), .width(32), .enable("false")) multiplexer_1 (
    .in0(adder_1_out), .in1(subtractor_1_out), .in2(multiplier_1_out), .in3(divider_1_out), .out(out_5),
    .sel(in_3[1:0]));
endmodule

module UC (
  input  [5:0] in_1,
  output reg_dest,
  output jump,
  output mem_to_reg,
  output [6:0] alu_op,
  output mem_write,
  output ula_src,
  output branch,
  output reg_write
);

  UC_IN uc_in_1 (
    .a(in_1[5]), .reg_dest(reg_dest), .b(in_1[4]), .jump(jump), .c(in_1[3]), .mem_to_reg(mem_to_reg),
    .d(in_1[2]), .uc_op6(alu_op[6]), .e(in_1[1]), .uc_op5(alu_op[5]), .f(in_1[0]), .uc_op4(alu_op[4]),
    .uc_op3(alu_op[3]), .uc_op2(alu_op[2]), .uc_op1(alu_op[1]), .uc_op0(alu_op[0]), .mem_write(mem_write),
    .ula_src(ula_src), .branch(branch), .reg_write(reg_write));
endmodule

module UC_IN (
  input  a,
  input  b,
  input  c,
  input  d,
  input  e,
  input  f,
  output reg_dest,
  output jump,
  output mem_to_reg,
  output uc_op6,
  output uc_op5,
  output uc_op4,
  output uc_op3,
  output uc_op2,
  output uc_op1,
  output uc_op0,
  output mem_write,
  output ula_src,
  output branch,
  output reg_write
);

  wire and_2_out, and_3_out, and_4_out, and_5_out, and_6_out, and_7_out, and_8_out, and_9_out, and_10_out,
       and_11_out, and_12_out, and_13_out, not_2_out, not_3_out, not_4_out, not_5_out, not_6_out, not_7_out,
       not_8_out, not_9_out, not_10_out, not_11_out, not_12_out, not_13_out, not_14_out, not_15_out,
       not_16_out;

  not not_1 (reg_dest, d);
  not not_2 (not_2_out, f);
  not not_3 (not_3_out, a);
  not not_4 (not_4_out, b);
  not not_5 (not_5_out, d);
  not not_6 (not_6_out, f);
  not not_7 (not_7_out, f);
  not not_8 (not_8_out, a);
  not not_9 (not_9_out, b);
  not not_10 (not_10_out, d);
  not not_11 (not_11_out, f);
  not not_12 (not_12_out, c);
  not not_13 (not_13_out, d);
  not not_14 (not_14_out, f);
  not not_15 (not_15_out, d);
  not not_16 (not_16_out, e);
  and and_1 (jump, d, not_2_out);
  and and_2 (and_2_out, not_3_out, not_4_out, c, not_5_out, not_6_out);
  and and_3 (and_3_out, c, not_7_out);
  and and_4 (and_4_out, c, e);
  and and_5 (and_5_out, c, d);
  and and_6 (and_6_out, b, c);
  and and_7 (and_7_out, a, c);
  and and_8 (and_8_out, not_8_out, not_9_out, c, not_10_out, not_11_out);
  and and_9 (and_9_out, not_12_out, not_13_out, not_14_out);
  and and_10 (and_10_out, not_15_out, e);
  and and_11 (and_11_out, d, not_16_out);
  and and_12 (and_12_out, d, f);
  and and_13 (and_13_out, c, d);
  or or_1 (uc_op0, e, and_2_out);
  or or_2 (mem_write, and_3_out, and_4_out, and_5_out, and_6_out, and_7_out);
  or or_3 (ula_src, e, and_8_out);
  or or_4 (reg_write, and_9_out, and_10_out, and_11_out, and_12_out, and_13_out, b, a);

  assign branch = 1'b1;
  assign mem_to_reg = e;
  assign uc_op1 = 1'b0;
  assign uc_op2 = 1'b0;
  assign uc_op3 = 1'b0;
  assign uc_op4 = 1'b0;
  assign uc_op5 = 1'b0;
  assign uc_op6 = 1'b0;
endmodule

module ula_control (
  input  [6:0] uc_op,
  input  [5:0] funct,
  output [5:0] out_3
);

  Multiplexer #(.width(6), .enable("false")) multiplexer_1 (.in0(funct), .in1(uc_op[6:1]), .out(out_3), .sel(uc_op[0]));
endmodule
